// Logisim project Attempt2.circ as structural Verilog: 8 circuits, main circuit OLD
module OLD (
  input  RESET,
  output [15:0] out_2,
  output [1:0] out_3,
  output [3:0] out_4,
  output [3:0] out_5,
  output [15:0] out_6
);

  wire control_unit_1_p3, control_unit_1_p4, MASTER_CLOCK_out, or_1_out;
  wire [3:0] control_unit_1_p2;
  wire [15:0] adder_1_out, alu_1_result, general_register_1_reg_a_out, general_register_1_reg_b_out,
       multiplexer_1_out, ram_1_data, register_1_q;

  Clock MASTER_CLOCK (.out(MASTER_CLOCK_out));
  Register #(.width(16)) register_1 (
    .D(adder_1_out), .Q(register_1_q), .clk(MASTER_CLOCK_out), .clr(RESET));  // open: en
  Adder #(.width(16)) adder_1 (.a(16'h1), .b(register_1_q), .out(adder_1_out));  // open: cin, cout
  ROM #(.addrWidth(16), .dataWidth(16)) rom_1 (.addr(register_1_q), .data(out_2));  // open: sel
  assign out_6 = {{8{1'b0}}, out_2[11:4]};  // Bit_Extender bit_extender_1
  // Control_unit control_unit_1: pin names not known; wires that end beside it: out_2[3:0], control_unit_1_p2, control_unit_1_p3, control_unit_1_p4, out_3[0], out_3[1]
  ALU alu_1 (
    .A(general_register_1_reg_a_out), .B(general_register_1_reg_b_out), .RESULT(alu_1_result),
    .SELECTOR(control_unit_1_p2));  // open: CARRY_ADD, CARRY_SUB, COMP, FLAG_STR, COMP_TYPE
  or or_1 (or_1_out, out_3[0], out_3[1], control_unit_1_p3);
  General_Register general_register_1 (
    .REG_WRITE(out_2[15:12]), .REG_DATA(multiplexer_1_out), .REG_A_OUT(general_register_1_reg_a_out),
    .REG_A_WRITE(out_2[7:4]), .REG_B_OUT(general_register_1_reg_b_out), .REG_B_WRITE(out_2[11:8]),
    .ENABLE_WRITE(or_1_out), .CLOCK(MASTER_CLOCK_out), .RESET(RESET));  // open: Number_Print
  RAM #(.addrWidth(16), .dataWidth(16), .bus("separate")) ram_1 (
    .data(ram_1_data), .str(control_unit_1_p4), .clk(MASTER_CLOCK_out), .ld(out_3[0]), .clr(RESET));  // open: addr, din, sel
  Multiplexer #(.select(2), .width(16)) multiplexer_1 (
    .in0(alu_1_result), .in1(ram_1_data), .in2(out_6), .out(multiplexer_1_out), .sel(out_3));  // open: in3, en

  assign out_4 = out_2[7:4];
  assign out_5 = out_2[11:8];

  // Notes on the sheet:
  //   PROGRAM_COUNTER
  //   ROM
  //   IMMEDIATE
  //   VALUE
  //   CURRENT_INSTRUCTION
  //   contents of rom_1 (hex, n*v repeats v):
  //   5a 104a 2105
  //   DECODE
  //   WRITE_CHECK
  //   RAM
  //   WHO_WRITES_CHECK
endmodule

module ALU (
  input  [3:0] SELECTOR,
  input  [15:0] A,
  input  [15:0] B,
  input  [2:0] COMP_TYPE,
  input  COMP,
  output [15:0] RESULT,
  output CARRY_ADD,
  output CARRY_SUB,
  output FLAG_STR
);

  wire comparator_1_eq, comparator_1_gt, comparator_1_lt, demultiplexer_1_out0, multiplexer_2_out, not_3_out,
       or_3_out, or_4_out;
  wire [15:0] adder_1_out, and_1_out, and_2_out, and_3_out, divider_1_out, multiplier_1_out, not_1_out,
       not_2_out, or_1_out, or_2_out, subtractor_1_out, undriven;

  Adder #(.width(16)) adder_1 (.a(A), .b(B), .out(adder_1_out), .cin(1'b0), .cout(CARRY_ADD));
  Subtractor #(.width(16)) subtractor_1 (.a(A), .b(B), .out(subtractor_1_out), .bin(1'b0), .bout(CARRY_SUB));
  Multiplier #(.width(16)) multiplier_1 (.a(A), .b(B), .out(multiplier_1_out));  // open: cin, cout
  Divider #(.width(16)) divider_1 (.a(A), .b(B), .out(divider_1_out));  // open: upper, rem
  Comparator #(.width(16)) comparator_1 (
    .a(A), .b(B), .gt(comparator_1_gt), .eq(comparator_1_eq), .lt(comparator_1_lt));
  assign and_1_out = A & B;  // AND_Gate and_1, 16 bits wide
  assign or_1_out = A | B;  // OR_Gate or_1, 16 bits wide
  assign or_2_out = A | B;  // OR_Gate or_2, 16 bits wide
  assign and_2_out = A & B;  // AND_Gate and_2, 16 bits wide
  assign not_1_out = ~and_2_out;  // NOT_Gate not_1, 16 bits wide
  assign not_2_out = ~and_3_out;  // NOT_Gate not_2, 16 bits wide
  assign and_3_out = or_2_out & not_1_out;  // AND_Gate and_3, 16 bits wide
  or or_3 (or_3_out, comparator_1_gt, comparator_1_eq);
  not not_3 (not_3_out, comparator_1_eq);
  or or_4 (or_4_out, comparator_1_eq, comparator_1_lt);
  Multiplexer #(.select(4), .width(16)) multiplexer_1 (
    .in0(undriven), .in1(and_1_out), .in2(or_1_out), .in3(and_3_out), .in4(not_2_out), .in5(adder_1_out),
    .in6(subtractor_1_out), .in7(multiplier_1_out), .in8(divider_1_out), .out(RESULT), .sel(SELECTOR));  // open: in9, in10, in11, in12, in13, in14, in15, en
  Multiplexer #(.select(3)) multiplexer_2 (
    .in0(comparator_1_gt), .in1(or_3_out), .in2(comparator_1_eq), .in3(not_3_out), .in4(or_4_out),
    .in5(comparator_1_lt), .in6(comparator_1_eq), .out(multiplexer_2_out), .sel(COMP_TYPE));  // open: in7, en
  Demultiplexer demultiplexer_1 (
    .out0(demultiplexer_1_out0), .out1(FLAG_STR), .in(multiplexer_2_out), .sel(COMP));  // open: en

  // Notes on the sheet:
  //   NOTHING
  //   AND -> 0001
  //   XOR -> 0011
  //   XNOR -> 0100
  //   SUB -> 0110
  //   DIV -> 1000
  //   OR -> 0010
  //   XOR -> 0011
  //   ADD -> 0101
  //   MUL -> 0111
endmodule

// CONTROL_UNIT
module Control_unit (
  input  [3:0] OPCode,
  output NO_OP,
  output COPY,
  output JUMP,
  output BOUNCER,
  output ALU_RUN,
  output WRITE,
  output [3:0] ALUOP,
  output JUMP_NZERO,
  output LOAD,
  output COMP
);

  wire comparator_1_eq, comparator_1_gt;

  Comparator #(.width(4), .mode("unsigned")) comparator_1 (
    .a(4'b1001), .b(OPCode), .gt(comparator_1_gt), .eq(comparator_1_eq));  // open: lt
  or or_1 (ALU_RUN, comparator_1_eq, comparator_1_gt);
  and and_1 (COMP, OPCode[0], ~OPCode[1], ~OPCode[2], OPCode[3]);  // AND_Gate
  and and_2 (LOAD, ~OPCode[0], OPCode[1], ~OPCode[2], OPCode[3]);  // AND_Gate
  and and_3 (JUMP_NZERO, OPCode[0], OPCode[1], ~OPCode[2], OPCode[3]);  // AND_Gate
  and and_4 (WRITE, ~OPCode[0], ~OPCode[1], OPCode[2], OPCode[3]);  // AND_Gate
  and and_5 (BOUNCER, OPCode[0], ~OPCode[1], OPCode[2], OPCode[3]);  // AND_Gate
  and and_6 (JUMP, ~OPCode[0], OPCode[1], OPCode[2], OPCode[3]);  // AND_Gate
  and and_7 (COPY, OPCode[0], OPCode[1], OPCode[2], OPCode[3]);
  and and_8 (NO_OP, ~OPCode[0], ~OPCode[1], ~OPCode[2], ~OPCode[3]);  // AND_Gate

  assign ALUOP = OPCode;

  // Notes on the sheet:
  //   SWAP REGISTER
  //   JUMPING
  //   STILL NEED!!!
  //   FLAG SETTING, ZERO, NON-NEGATIVE (WILL NEED SIGNED)
  //   SIGNED
  //   terminate program when 000f is met in RAM
  //   Hex
  //   Binary
  //   0
  //   0000
  //   1
  //   0001
  //   2
  //   0010
  //   0011
  //   3
  //   0100
  //   4
  //   5
  //   0101
  //   6
  //   0110
  //   7
  //   0111
  //   8
  //   1000
  //   9
  //   1001
  //   a
  //   1010
  //   b
  //   1011
  //   c
  //   1100
  //   d
  //   1101
  //   e
  //   1110
  //   f
  //   1111
  //   OPCode_Instructions
  //   No_Operation
  //   AND
  //   OR
  //   XOR
  //   XNOR
  //   ADD
  //   LOAD
  //   JUMP_NZERO
  //   WRITE
  //   BOUNCER
  //   JUMP
  //   COPY
  //   SUB
  //   MUL
  //   DIV
  //   COMP
endmodule

// GENERAL_REGISTER
module General_Register (
  input  [3:0] REG_A_WRITE,
  input  [3:0] REG_B_WRITE,
  input  [3:0] REG_WRITE,
  input  [15:0] REG_DATA,
  input  ENABLE_WRITE,
  input  CLOCK,
  input  RESET,
  output [15:0] REG_A_OUT,
  output [15:0] REG_B_OUT,
  output [15:0] Number_Print
);

  wire and_1_out, and_2_out, and_3_out, and_4_out, and_5_out, and_6_out, and_7_out, and_8_out, and_9_out,
       and_10_out, and_11_out, and_12_out, and_15_out, and_16_out, R0, R1, R2, R3, R4, R5, R6, R7, R8, R9,
       R10, R11, R12, R13, R14, R15;
  wire [15:0] OUT0, OUT1, OUT2, OUT3, OUT4, OUT5, OUT6, OUT7, OUT8, OUT9, OUT10, OUT11, OUT12, OUT13, OUT15;

  Decoder #(.select(4)) decoder_1 (
    .out0(R0), .out1(R1), .out2(R2), .out3(R3), .out4(R4), .out5(R5), .out6(R6), .out7(R7), .out8(R8),
    .out9(R9), .out10(R10), .out11(R11), .out12(R12), .out13(R13), .out14(R14), .out15(R15), .sel(REG_WRITE));  // open: en
  and and_1 (and_1_out, R0, ENABLE_WRITE);
  and and_2 (and_2_out, R1, ENABLE_WRITE);
  and and_3 (and_3_out, R2, ENABLE_WRITE);
  and and_4 (and_4_out, R3, ENABLE_WRITE);
  and and_5 (and_5_out, R4, ENABLE_WRITE);
  and and_6 (and_6_out, R5, ENABLE_WRITE);
  and and_7 (and_7_out, R6, ENABLE_WRITE);
  and and_8 (and_8_out, R7, ENABLE_WRITE);
  Register #(.width(16)) u_R0 (.D(REG_DATA), .en(and_1_out), .Q(OUT0), .clk(CLOCK), .clr(RESET));
  Register #(.width(16)) u_R1 (.D(REG_DATA), .en(and_2_out), .Q(OUT1), .clk(CLOCK), .clr(RESET));
  Register #(.width(16)) u_R2 (.D(REG_DATA), .en(and_3_out), .Q(OUT2), .clk(CLOCK), .clr(RESET));
  Register #(.width(16)) u_R3 (.D(REG_DATA), .en(and_4_out), .Q(OUT3), .clk(CLOCK), .clr(RESET));
  Register #(.width(16)) u_R4 (.D(REG_DATA), .en(and_5_out), .Q(OUT4), .clk(CLOCK), .clr(RESET));
  Register #(.width(16)) u_R5 (.D(REG_DATA), .en(and_6_out), .Q(OUT5), .clk(CLOCK), .clr(RESET));
  Register #(.width(16)) u_R6 (.D(REG_DATA), .en(and_7_out), .Q(OUT6), .clk(CLOCK), .clr(RESET));
  Register #(.width(16)) u_R7 (.D(REG_DATA), .en(and_8_out), .Q(OUT7), .clk(CLOCK), .clr(RESET));
  and and_9 (and_9_out, R8, ENABLE_WRITE);
  and and_10 (and_10_out, R9, ENABLE_WRITE);
  and and_11 (and_11_out, R10, ENABLE_WRITE);
  and and_12 (and_12_out, R11, ENABLE_WRITE);
  // AND_Gate and_13 has open pins: in0=R12, in1=ENABLE_WRITE, out=open
  // AND_Gate and_14 has open pins: in0=R13, in1=ENABLE_WRITE, out=open
  and and_15 (and_15_out, R14, ENABLE_WRITE);
  and and_16 (and_16_out, R15, ENABLE_WRITE);
  Register #(.width(16)) u_R8 (.D(REG_DATA), .en(and_9_out), .Q(OUT8), .clk(CLOCK), .clr(RESET));
  Register #(.width(16)) u_R9 (.D(REG_DATA), .en(and_10_out), .Q(OUT9), .clk(CLOCK), .clr(RESET));
  Register #(.width(16)) u_R10 (.D(REG_DATA), .en(and_11_out), .Q(OUT10), .clk(CLOCK), .clr(RESET));
  Register #(.width(16)) u_R11 (.D(REG_DATA), .en(and_12_out), .Q(OUT11), .clk(CLOCK), .clr(RESET));
  Register #(.width(16)) RZERO (.Q(OUT12), .clk(ENABLE_WRITE), .clr(RESET));  // open: D, en
  Register #(.width(16)) RINC (.D(16'h1), .Q(OUT13), .clk(ENABLE_WRITE), .clr(RESET));  // open: en
  Register #(.width(16)) RDIS (.D(REG_DATA), .en(and_15_out), .Q(Number_Print), .clk(CLOCK), .clr(RESET));
  Register #(.width(16)) RSTA (.D(REG_DATA), .en(and_16_out), .Q(OUT15), .clk(CLOCK), .clr(RESET));
  Multiplexer #(.select(4), .width(16)) multiplexer_1 (
    .in0(OUT0), .in1(OUT1), .in2(OUT2), .in3(OUT3), .in4(OUT4), .in5(OUT5), .in6(OUT6), .in7(OUT7),
    .in8(OUT8), .in9(OUT9), .in10(OUT10), .in11(OUT11), .in12(OUT12), .in13(OUT13), .in14(Number_Print),
    .in15(OUT15), .out(REG_A_OUT), .sel(REG_A_WRITE));  // open: en
  Multiplexer #(.select(4), .width(16)) multiplexer_2 (
    .in0(OUT0), .in1(OUT1), .in2(OUT2), .in3(OUT3), .in4(OUT4), .in5(OUT5), .in6(OUT6), .in7(OUT7),
    .in8(OUT8), .in9(OUT9), .in10(OUT10), .in11(OUT11), .in12(OUT12), .in13(OUT13), .in14(Number_Print),
    .in15(OUT15), .out(REG_B_OUT), .sel(REG_B_WRITE));  // open: en

  // Other names for the same wires on the sheet: OUT14[15:0] = Number_Print
endmodule

module CPU (
  input  MANUAL_RESET,
  output [1:0] out_2,
  output [15:0] out_3,
  output [15:0] ROM_VAL,
  output [1:0] out_5,
  output [15:0] RAM_VAL
);

  wire _0a, _0b, _0c, _0d, _0e, _0f, _0g, _1a, _1b, _1c, _1d, _1e, _1f, _1g, _2a, _2b, _2c, _2d, _2e, _2f,
       _2g, _3a, _3b, _3c, _3d, _3e, _3f, _3g, _4a, _4b, _4c, _4d, _4e, _4f, _4g, alu_1_carry_add,
       alu_1_carry_sub, alu_1_flag_str, AUTO_RESET_q, BOUNCER, CLOCK, control_unit_1_alu_run,
       control_unit_1_bouncer, control_unit_1_comp, control_unit_1_copy, control_unit_1_jump,
       control_unit_1_jump_nzero, control_unit_1_load, control_unit_1_write, d_ff_3_q, demultiplexer_4_out0,
       F_AND, F_OR, JUMP, JUMP_NZERO, multiplexer_2_out, multiplexer_15_out, or_3_out, or_5_out, or_6_out,
       or_7_out, or_8_out, or_9_out, RESET, RESET_2, RESET_3, SEND_CHECK, xor_1_out, ZERO;
  wire [1:0] or_2_out;
  wire [3:0] control_unit_1_aluop, Double_Dabble_prime_out0, Double_Dabble_prime_out1,
       Double_Dabble_prime_out2, Double_Dabble_prime_out3, Double_Dabble_prime_out4, multiplexer_8_out,
       multiplexer_12_out;
  wire [7:0] BOUNCE_DTR;
  wire [15:0] alu_1_result, B_RES, bit_extender_1_out, bit_extender_2_out, demultiplexer_1_out1,
       demultiplexer_2_out0, demultiplexer_2_out1, demultiplexer_3_out1, general_register_1_number_print,
       multiplexer_4_out, multiplexer_5_out, multiplexer_6_out, multiplexer_7_out, multiplexer_9_out,
       multiplexer_10_out, PC, R_MEM, register_1_q, rom_1_data;
  wire [15:8] R_VAL;

  Multiplexer #(.width(16)) multiplexer_1 (
    .in0({RAM_VAL[11:4], BOUNCE_DTR}), .in1(PC), .out(out_3), .sel(ZERO));  // open: en
  Multiplexer multiplexer_2 (.in0(F_AND), .in1(F_OR), .out(multiplexer_2_out), .sel(SEND_CHECK));  // open: en
  Multiplexer #(.width(16)) multiplexer_3 (
    .in0(PC), .in1({RAM_VAL[11:4], BOUNCE_DTR}), .out(B_RES), .sel(multiplexer_2_out));  // open: en
  Clock #(.highDuration(64), .lowDuration(64)) MASTER_CLOCK (.out(CLOCK));
  Multiplexer #(.select(2), .width(16)) multiplexer_4 (
    .in0(PC), .in1({RAM_VAL[11:4], BOUNCE_DTR}), .in2(B_RES), .in3(out_3), .out(multiplexer_4_out),
    .sel(or_2_out));  // open: en
  or or_1 (or_2_out[1], BOUNCER, JUMP_NZERO);
  or or_2 (or_2_out[0], JUMP, JUMP_NZERO);
  xor xor_1 (xor_1_out, demultiplexer_4_out0, out_2[0]);
  Register #(.width(16)) register_1 (.D(multiplexer_4_out), .Q(register_1_q), .clk(CLOCK), .clr(or_3_out));  // open: en
  Demultiplexer #(.width(16)) demultiplexer_1 (
    .out1(demultiplexer_1_out1), .in(register_1_q), .sel(out_2[0]));  // open: out0, en
  or or_3 (or_3_out, RESET_2, d_ff_3_q);
  or or_4 (RESET_2, AUTO_RESET_q, MANUAL_RESET);
  D_Flip_Flop AUTO_RESET (.clk(CLOCK), .D(RESET_3), .Q(AUTO_RESET_q));  // open: Qn, preset, en, reset
  D_Flip_Flop d_ff_1 (.clk(CLOCK), .D(xor_1_out), .Q(out_2[0]), .reset(RESET_2));  // open: Qn, preset, en
  Adder #(.width(16)) adder_1 (.a(16'h1), .b(register_1_q), .out(PC));  // open: cin, cout
  Demultiplexer #(.width(16)) demultiplexer_2 (
    .out0(demultiplexer_2_out0), .out1(demultiplexer_2_out1), .in(register_1_q), .sel(out_2[1]));  // open: en
  and and_1 (RESET, out_2[0], demultiplexer_4_out0);
  D_Flip_Flop d_ff_2 (.clk(CLOCK), .D(or_5_out), .Q(out_2[1]), .reset(RESET_2));  // open: Qn, preset, en
  or or_5 (or_5_out, out_2[1], RESET);
  Multiplexer #(.width(16)) multiplexer_5 (
    .in0(demultiplexer_1_out1), .in1(demultiplexer_2_out1), .out(multiplexer_5_out), .sel(out_2[1]));  // open: en
  Demultiplexer #(.width(16)) demultiplexer_3 (
    .out0(ROM_VAL), .out1(demultiplexer_3_out1), .in(rom_1_data), .sel(out_2[0]));  // open: en
  ROM #(.addrWidth(16), .dataWidth(16)) rom_1 (.addr(demultiplexer_2_out0), .data(rom_1_data));  // open: sel
  Multiplexer #(.width(16)) multiplexer_6 (
    .in0(multiplexer_5_out), .in1(R_MEM), .out(multiplexer_6_out), .sel(control_unit_1_write));  // open: en
  D_Flip_Flop d_ff_3 (.clk(CLOCK), .D(RESET), .Q(d_ff_3_q), .reset(RESET_2));  // open: Qn, preset, en
  Multiplexer #(.width(16)) multiplexer_7 (
    .in0(demultiplexer_3_out1), .in1({R_VAL, BOUNCE_DTR}), .out(multiplexer_7_out), .sel(control_unit_1_write));  // open: en
  or or_6 (or_6_out, control_unit_1_write, out_2[0]);
  RAM #(.addrWidth(16), .dataWidth(16), .bus("separate")) ram_1 (
    .addr(multiplexer_6_out), .din(multiplexer_7_out), .data(RAM_VAL), .str(or_6_out), .clk(CLOCK),
    .clr(RESET_2));  // open: sel, ld
  Multiplexer #(.select(2), .width(4)) multiplexer_8 (
    .in0(ROM_VAL[3:0]), .in1(demultiplexer_3_out1[3:0]), .in2(RAM_VAL[3:0]), .out(multiplexer_8_out),
    .sel(out_2));  // open: in3, en
  assign bit_extender_1_out = {{8{1'b0}}, ROM_VAL[11:4]};  // Bit_Extender bit_extender_1
  Demultiplexer demultiplexer_4 (
    .out0(demultiplexer_4_out0), .out1(RESET_3), .in(control_unit_1_copy), .sel(out_2[1]));  // open: en
  Control_unit control_unit_1 (
    .OPCode(multiplexer_8_out), .COPY(control_unit_1_copy), .JUMP(control_unit_1_jump),
    .BOUNCER(control_unit_1_bouncer), .WRITE(control_unit_1_write), .LOAD(control_unit_1_load),
    .ALUOP(control_unit_1_aluop), .ALU_RUN(control_unit_1_alu_run), .JUMP_NZERO(control_unit_1_jump_nzero),
    .COMP(control_unit_1_comp));  // open: NO_OP
  Multiplexer #(.width(16)) multiplexer_9 (
    .in0(alu_1_result), .in1(multiplexer_10_out), .out(multiplexer_9_out), .sel(control_unit_1_load));  // open: en
  Multiplexer #(.width(16)) multiplexer_10 (
    .in0(bit_extender_1_out), .in1(bit_extender_2_out), .out(multiplexer_10_out), .sel(out_2[1]));  // open: en
  assign bit_extender_2_out = {{8{1'b0}}, RAM_VAL[11:4]};  // Bit_Extender bit_extender_2
  Multiplexer multiplexer_11 (.in0(1'b0), .in1(control_unit_1_jump), .out(JUMP), .sel(out_2[1]));  // open: en
  Multiplexer #(.width(4)) multiplexer_12 (
    .in0(RAM_VAL[7:4]), .in1(RAM_VAL[15:12]), .out(multiplexer_12_out), .sel(or_7_out));  // open: en
  or or_7 (or_7_out, JUMP, JUMP_NZERO, BOUNCER);
  Multiplexer multiplexer_13 (.in0(1'b0), .in1(control_unit_1_bouncer), .out(BOUNCER), .sel(out_2[1]));  // open: en
  ALU alu_1 (
    .A({R_VAL, BOUNCE_DTR}), .B(R_MEM), .CARRY_ADD(alu_1_carry_add), .CARRY_SUB(alu_1_carry_sub),
    .RESULT(alu_1_result), .SELECTOR(control_unit_1_aluop), .COMP(control_unit_1_comp),
    .FLAG_STR(alu_1_flag_str), .COMP_TYPE(RAM_VAL[14:12]));
  General_Register general_register_1 (
    .REG_WRITE(RAM_VAL[15:12]), .REG_DATA(multiplexer_9_out), .REG_A_OUT({R_VAL, BOUNCE_DTR}),
    .REG_A_WRITE(multiplexer_12_out), .REG_B_OUT(R_MEM), .REG_B_WRITE(RAM_VAL[11:8]),
    .ENABLE_WRITE(or_8_out), .CLOCK(CLOCK), .RESET(RESET_2), .Number_Print(general_register_1_number_print));
  or or_8 (or_8_out, control_unit_1_load, control_unit_1_alu_run);
  Multiplexer multiplexer_14 (
    .in0(1'b0), .in1(control_unit_1_jump_nzero), .out(JUMP_NZERO), .sel(out_2[1]));  // open: en
  Multiplexer multiplexer_15 (
    .in0(1'b0), .in1(control_unit_1_comp), .out(multiplexer_15_out), .sel(out_2[1]));  // open: en
  Flag_Register flag_register_1 (
    .AND_OR(RAM_VAL[15]), .CARRY(or_9_out), .ENABLE_COMP(multiplexer_15_out), .CLOCK(CLOCK), .RESET(RESET_2),
    .CURR_FLAG(alu_1_flag_str), .COMPARISONS(RAM_VAL[14:12]), .ZERO_RES(ZERO), .SEND_TYPE(SEND_CHECK),
    .AND(F_AND), .OR(F_OR));
  or or_9 (or_9_out, alu_1_carry_add, alu_1_carry_sub);
  Digit_Chooser BCD (.a(_0a), .b(_0b), .c(_0c), .d(_0d), .e(_0e), .f(_0f), .g(_0g), .Digit(Double_Dabble_prime_out4));
  BinaryToBCD Double_Dabble_prime (
    .Reg_Val(general_register_1_number_print), .CLOCK(CLOCK), .RESET(RESET_2),
    .Out0(Double_Dabble_prime_out0), .Out1(Double_Dabble_prime_out1), .Out2(Double_Dabble_prime_out2),
    .Out3(Double_Dabble_prime_out3), .Out4(Double_Dabble_prime_out4));
  Digit_Chooser BCD_2 (.a(_1a), .b(_1b), .c(_1c), .d(_1d), .e(_1e), .f(_1f), .g(_1g), .Digit(Double_Dabble_prime_out3));
  _7_Segment_Display u_7_segment_display_1 (.g(_0a), .f(_0b), .a(_0c), .b(_0d), .e(_0e), .d(_0f), .c(_0g));  // open: dp
  Digit_Chooser BCD_3 (.a(_2a), .b(_2b), .c(_2c), .d(_2d), .e(_2e), .f(_2f), .g(_2g), .Digit(Double_Dabble_prime_out2));
  _7_Segment_Display u_7_segment_display_2 (.g(_1a), .f(_1b), .a(_1c), .b(_1d), .e(_1e), .d(_1f), .c(_1g));  // open: dp
  _7_Segment_Display u_7_segment_display_3 (.g(_2a), .f(_2b), .a(_2c), .b(_2d), .e(_2e), .d(_2f), .c(_2g));  // open: dp
  _7_Segment_Display u_7_segment_display_4 (.g(_3a), .f(_3b), .a(_3c), .b(_3d), .e(_3e), .d(_3f), .c(_3g));  // open: dp
  Digit_Chooser BCD_4 (.a(_3a), .b(_3b), .c(_3c), .d(_3d), .e(_3e), .f(_3f), .g(_3g), .Digit(Double_Dabble_prime_out1));
  _7_Segment_Display u_7_segment_display_5 (.g(_4a), .f(_4b), .a(_4c), .b(_4d), .e(_4e), .d(_4f), .c(_4g));  // open: dp
  Digit_Chooser BCD_5 (.a(_4a), .b(_4b), .c(_4c), .d(_4d), .e(_4e), .f(_4f), .g(_4g), .Digit(Double_Dabble_prime_out0));

  // Other names for the same wires on the sheet: BOUNCE_DTR[15:8] = RAM_VAL[11:4]; JUMP_H[7:0] = RAM_VAL[11:4];
  //   RAM_ON = out_2[1]; JUMP_L[7:0] = BOUNCE_DTR; R_VAL[7:0] = BOUNCE_DTR; COMP_TYPE[2:0] = RAM_VAL[14:12];
  //   AND_OR = RAM_VAL[15]; STR_RAM = RESET

  // Notes on the sheet:
  //   PROGRAM_COUNTER
  //   Copy_To_RAM_ State
  //   ROM
  //   RESET_PC_FOR_RAM
  //   contents of rom_1 (hex, n*v repeats v):
  //   f e0aa 103a ede6 1ce9 100d f
  //   RAM_ACTIVE
  //   OPCODE_SIGNALS
  //   ROM_IMMEDIATE
  //   RAM
  //   RAM_IMMEDIATE
  //   WRITE_ACTIVE
  //   VISUAL_DISPLAY
endmodule

module BinaryToBCD (
  input  [15:0] Reg_Val,
  input  CLOCK,
  input  RESET,
  output [3:0] Out2,
  output [3:0] Out3,
  output [3:0] Out4,
  output [3:0] Out0,
  output [3:0] Out1
);

  wire and_2_out, and_3_out, and_4_out, and_5_out, and_6_out, clk, clock_1_out, clr, comparator_1_lt,
       comparator_2_gt, comparator_3_gt, comparator_4_gt, comparator_5_gt, comparator_6_gt, not_1_out,
       not_2_out, not_3_out, not_4_out, not_5_out, not_6_out, shift, shift_register_1_out,
       shift_register_2_out, shift_register_3_out, shift_register_4_out, shift_register_5_out;
  wire [3:0] adder_2_out, adder_3_out, adder_4_out, adder_5_out, adder_6_out, shift_register_2_q0,
       shift_register_3_q0, shift_register_4_q0, shift_register_5_q0, shift_register_6_q0;
  wire [7:0] adder_1_out, register_1_q;

  _7_Segment_Display u_7_segment_display_1 (.g(1'b1), .f(1'b1), .a(1'b1), .b(1'b1), .c(1'b1));  // open: e, d, dp
  // Probe on Reg_Val
  or or_1 (clr, CLOCK, RESET);
  Adder adder_1 (.a(register_1_q), .b(8'h1), .out(adder_1_out));  // open: cin, cout
  not not_1 (not_1_out, shift);
  Shift_Register #(.length(16)) shift_register_1 (
    .shift(shift), .clk(clk), .out(shift_register_1_out), .load(CLOCK), .clr(RESET), .d0(Reg_Val[0]),
    .d1(Reg_Val[1]), .d2(Reg_Val[2]), .d3(Reg_Val[3]), .d4(Reg_Val[4]), .d5(Reg_Val[5]), .d6(Reg_Val[6]),
    .d7(Reg_Val[7]), .d8(Reg_Val[8]), .d9(Reg_Val[9]), .d10(Reg_Val[10]), .d11(Reg_Val[11]),
    .d12(Reg_Val[12]), .d13(Reg_Val[13]), .d14(Reg_Val[14]), .d15(Reg_Val[15]));  // open: in, q0, q1, q2, q3, q4, q5, q6, q7, q8, q9, q10, q11, q12, q13, q14, q15
  J_K_Flip_Flop j_k_ff_1 (.J(1'b1), .clk(clk), .K(1'b1), .Q(shift), .en(1'b1), .reset(clr));  // open: Qn, preset
  Register register_1 (.D(adder_1_out), .Q(register_1_q), .clk(not_1_out), .clr(clr));  // open: en
  Comparator comparator_1 (.a(register_1_q), .b(8'h16), .lt(comparator_1_lt));  // open: gt, eq
  Clock clock_1 (.out(clock_1_out));
  and and_1 (clk, comparator_1_lt, clock_1_out);
  Shift_Register #(.length(4)) shift_register_2 (
    .shift(shift), .in(shift_register_1_out), .clk(clk), .out(shift_register_2_out), .load(and_2_out),
    .clr(clr), .d0(adder_2_out[0]), .q0(shift_register_2_q0[0]), .d1(adder_2_out[1]),
    .q1(shift_register_2_q0[1]), .d2(adder_2_out[2]), .q2(shift_register_2_q0[2]), .d3(adder_2_out[3]),
    .q3(shift_register_2_q0[3]));
  Comparator #(.width(4), .mode("unsigned")) comparator_2 (
    .a(shift_register_2_q0), .b(4'b0100), .gt(comparator_2_gt));  // open: eq, lt
  Adder #(.width(4)) adder_2 (.a(shift_register_2_q0), .b(4'b0011), .out(adder_2_out));  // open: cin, cout
  Register #(.width(4)) Digit0 (.D(shift_register_2_q0), .Q(Out0), .clk(CLOCK));  // open: en, clr
  and and_2 (and_2_out, comparator_2_gt, not_2_out);
  not not_2 (not_2_out, shift);
  // Probe on shift_register_6_q0
  // Probe on shift_register_5_q0
  // Probe on shift_register_4_q0
  // Probe on shift_register_3_q0
  Shift_Register #(.length(4)) shift_register_3 (
    .shift(shift), .in(shift_register_2_out), .clk(clk), .out(shift_register_3_out), .load(and_3_out),
    .clr(clr), .d0(adder_3_out[0]), .q0(shift_register_3_q0[0]), .d1(adder_3_out[1]),
    .q1(shift_register_3_q0[1]), .d2(adder_3_out[2]), .q2(shift_register_3_q0[2]), .d3(adder_3_out[3]),
    .q3(shift_register_3_q0[3]));
  // Probe on shift_register_2_q0
  Comparator #(.width(4), .mode("unsigned")) comparator_3 (
    .a(shift_register_3_q0), .b(4'b0100), .gt(comparator_3_gt));  // open: eq, lt
  Adder #(.width(4)) adder_3 (.a(shift_register_3_q0), .b(4'b0011), .out(adder_3_out));  // open: cin, cout
  Register #(.width(4)) Digit1 (.D(shift_register_3_q0), .Q(Out1), .clk(CLOCK));  // open: en, clr
  and and_3 (and_3_out, comparator_3_gt, not_3_out);
  not not_3 (not_3_out, shift);
  Shift_Register #(.length(4)) shift_register_4 (
    .shift(shift), .in(shift_register_3_out), .clk(clk), .out(shift_register_4_out), .load(and_4_out),
    .clr(clr), .d0(adder_4_out[0]), .q0(shift_register_4_q0[0]), .d1(adder_4_out[1]),
    .q1(shift_register_4_q0[1]), .d2(adder_4_out[2]), .q2(shift_register_4_q0[2]), .d3(adder_4_out[3]),
    .q3(shift_register_4_q0[3]));
  Comparator #(.width(4), .mode("unsigned")) comparator_4 (
    .a(shift_register_4_q0), .b(4'b0100), .gt(comparator_4_gt));  // open: eq, lt
  Adder #(.width(4)) adder_4 (.a(shift_register_4_q0), .b(4'b0011), .out(adder_4_out));  // open: cin, cout
  Register #(.width(4)) Digit2 (.D(shift_register_4_q0), .Q(Out2), .clk(CLOCK));  // open: en, clr
  and and_4 (and_4_out, comparator_4_gt, not_4_out);
  not not_4 (not_4_out, shift);
  Shift_Register #(.length(4)) shift_register_5 (
    .shift(shift), .in(shift_register_4_out), .clk(clk), .out(shift_register_5_out), .load(and_5_out),
    .clr(clr), .d0(adder_5_out[0]), .q0(shift_register_5_q0[0]), .d1(adder_5_out[1]),
    .q1(shift_register_5_q0[1]), .d2(adder_5_out[2]), .q2(shift_register_5_q0[2]), .d3(adder_5_out[3]),
    .q3(shift_register_5_q0[3]));
  Comparator #(.width(4), .mode("unsigned")) comparator_5 (
    .a(shift_register_5_q0), .b(4'b0100), .gt(comparator_5_gt));  // open: eq, lt
  Adder #(.width(4)) adder_5 (.a(shift_register_5_q0), .b(4'b0011), .out(adder_5_out));  // open: cin, cout
  Register #(.width(4)) Digit3 (.D(shift_register_5_q0), .Q(Out3), .clk(CLOCK));  // open: en, clr
  and and_5 (and_5_out, comparator_5_gt, not_5_out);
  not not_5 (not_5_out, shift);
  Shift_Register #(.length(4)) shift_register_6 (
    .shift(shift), .in(shift_register_5_out), .clk(clk), .load(and_6_out), .clr(clr), .d0(adder_6_out[0]),
    .q0(shift_register_6_q0[0]), .d1(adder_6_out[1]), .q1(shift_register_6_q0[1]), .d2(adder_6_out[2]),
    .q2(shift_register_6_q0[2]), .d3(adder_6_out[3]), .q3(shift_register_6_q0[3]));  // open: out
  and and_6 (and_6_out, comparator_6_gt, not_6_out);
  not not_6 (not_6_out, shift);
  Comparator #(.width(4), .mode("unsigned")) comparator_6 (
    .a(shift_register_6_q0), .b(4'b0100), .gt(comparator_6_gt));  // open: eq, lt
  Adder #(.width(4)) adder_6 (.a(shift_register_6_q0), .b(4'b0011), .out(adder_6_out));  // open: cin, cout
  Register #(.width(4)) Digit4 (.D(shift_register_6_q0), .Q(Out4), .clk(CLOCK));  // open: en, clr

  // Other names for the same wires on the sheet: Output = CLOCK
endmodule

// CONV
module Digit_Chooser (
  input  [3:0] Digit,
  output a,
  output b,
  output c,
  output d,
  output e,
  output f,
  output g
);

  wire and_1_out, and_2_out, and_3_out, and_4_out, and_5_out, and_6_out, and_7_out, and_8_out, and_9_out,
       and_10_out, and_11_out, and_12_out, and_13_out, and_14_out, and_15_out, and_16_out, not_1_out,
       not_2_out, not_3_out, not_4_out, not_5_out, not_6_out, not_7_out, not_8_out, not_9_out, not_10_out,
       not_11_out, not_12_out, not_13_out, not_14_out, not_15_out, not_16_out, not_17_out, not_18_out,
       not_19_out, not_20_out, not_21_out;

  not not_1 (not_1_out, Digit[2]);
  not not_2 (not_2_out, Digit[1]);
  not not_3 (not_3_out, Digit[0]);
  not not_4 (not_4_out, Digit[1]);
  not not_5 (not_5_out, Digit[0]);
  not not_6 (not_6_out, Digit[1]);
  not not_7 (not_7_out, Digit[0]);
  not not_8 (not_8_out, Digit[2]);
  not not_9 (not_9_out, Digit[0]);
  not not_10 (not_10_out, Digit[1]);
  not not_11 (not_11_out, Digit[0]);
  not not_12 (not_12_out, Digit[2]);
  not not_13 (not_13_out, Digit[0]);
  not not_14 (not_14_out, Digit[0]);
  not not_15 (not_15_out, Digit[2]);
  not not_16 (not_16_out, Digit[0]);
  not not_17 (not_17_out, Digit[2]);
  not not_18 (not_18_out, Digit[0]);
  not not_19 (not_19_out, Digit[1]);
  not not_20 (not_20_out, Digit[1]);
  and and_1 (and_1_out, not_1_out, Digit[1]);
  and and_2 (and_2_out, Digit[2], not_2_out);
  and and_3 (and_3_out, Digit[2], not_3_out);
  and and_4 (and_4_out, not_4_out, not_5_out);
  and and_5 (and_5_out, Digit[2], not_6_out);
  and and_6 (and_6_out, Digit[2], not_7_out);
  and and_7 (and_7_out, not_8_out, not_9_out);
  and and_8 (and_8_out, Digit[2], Digit[0]);
  not not_21 (not_21_out, Digit[2]);
  and and_9 (and_9_out, not_10_out, not_11_out);
  and and_10 (and_10_out, Digit[1], Digit[0]);
  and and_11 (and_11_out, not_12_out, not_13_out);
  and and_12 (and_12_out, Digit[1], not_14_out);
  and and_13 (and_13_out, not_15_out, not_16_out);
  and and_14 (and_14_out, not_17_out, Digit[1]);
  and and_15 (and_15_out, Digit[1], not_18_out);
  and and_16 (and_16_out, Digit[2], not_19_out, Digit[0]);
  or or_1 (g, not_20_out, Digit[0], Digit[2]);
  or or_2 (a, and_1_out, and_2_out, and_3_out, Digit[3]);
  or or_3 (b, and_4_out, and_5_out, and_6_out, Digit[3]);
  or or_4 (c, and_7_out, Digit[1], and_8_out, Digit[3]);
  or or_5 (d, not_21_out, and_9_out, and_10_out);
  or or_6 (e, and_11_out, and_12_out);
  or or_7 (f, and_13_out, and_14_out, and_15_out, and_16_out);
endmodule

// FLAG_REGISTER
module Flag_Register (
  input  CURR_FLAG,
  input  AND_OR,
  input  CARRY,
  input  [2:0] COMPARISONS,
  input  ENABLE_COMP,
  input  CLOCK,
  input  RESET,
  output SEND_TYPE,
  output AND,
  output OR,
  output ZERO_RES
);

  wire and_1_out, and_2_out, AND_3_q, decoder_1_out0, decoder_1_out1, decoder_1_out2, decoder_1_out3,
       decoder_1_out4, decoder_1_out5, decoder_1_out6, demultiplexer_1_out0, demultiplexer_1_out1,
       demultiplexer_2_out0, demultiplexer_3_out1, not_1_out, or_1_out, or_2_out, or_3_out;

  Decoder #(.select(3)) decoder_1 (
    .out0(decoder_1_out0), .out1(decoder_1_out1), .out2(decoder_1_out2), .out3(decoder_1_out3),
    .out4(decoder_1_out4), .out5(decoder_1_out5), .out6(decoder_1_out6), .sel(COMPARISONS));  // open: out7, en
  or or_1 (or_1_out, decoder_1_out0, decoder_1_out1, decoder_1_out2, decoder_1_out3, decoder_1_out4, decoder_1_out5);
  and and_1 (and_1_out, CURR_FLAG, or_1_out);
  Demultiplexer demultiplexer_1 (
    .out0(demultiplexer_1_out0), .out1(demultiplexer_1_out1), .in(and_1_out), .sel(AND_OR));  // open: en
  not not_1 (not_1_out, demultiplexer_1_out0);
  and and_2 (and_2_out, decoder_1_out6, CURR_FLAG);
  or or_2 (or_2_out, not_1_out, AND_3_q);
  D_Flip_Flop AND_3 (
    .clk(CLOCK), .D(or_2_out), .Q(AND_3_q), .en(demultiplexer_2_out0), .reset(RESET));  // open: Qn, preset
  Demultiplexer demultiplexer_2 (.out0(demultiplexer_2_out0), .in(ENABLE_COMP), .sel(AND_OR));  // open: out1, en
  not not_2 (AND, AND_3_q);
  or or_3 (or_3_out, demultiplexer_1_out1, OR);
  Demultiplexer demultiplexer_3 (.out1(demultiplexer_3_out1), .in(ENABLE_COMP), .sel(AND_OR));  // open: out0, en
  D_Flip_Flop OR_4 (.clk(CLOCK), .D(or_3_out), .Q(OR), .en(demultiplexer_3_out1), .reset(RESET));  // open: Qn, preset
  D_Flip_Flop u_SEND_TYPE (
    .clk(CLOCK), .D(AND_OR), .Q(SEND_TYPE), .en(ENABLE_COMP), .reset(RESET));  // open: Qn, preset
  D_Flip_Flop u_CARRY (.clk(CLOCK), .en(ENABLE_COMP), .reset(RESET));  // open: D, Q, Qn, preset
  D_Flip_Flop ZERO (.clk(CLOCK), .D(and_2_out), .Q(ZERO_RES), .en(ENABLE_COMP), .reset(RESET));  // open: Qn, preset

  // Notes on the sheet:
  //   AND HAS INVERTED LOGIC TO MAKE RESET SIMPLER
  //   Store compount results and check for both AND and OR active
  //   FOR AND -> 0 = 1 AND 1 = 0 FOR VALIDITY
endmodule
